# Fritzing sketch miljomataren (saved by Fritzing 0.9.6b)
breadboards: 1

parts:
  MKR_GSM = Arduino MKR1000
  LCD = LCD screen
  GPS = u-blox NEO-6M GPS Breakout
  R1 = Resistor [tolerance=±5% resistance=220 package="1206 [SMD]"]

nets:
  N1: MKR_GSM.D2_PWM, LCD.DB7
  N2: MKR_GSM.D3_PWM, LCD.DB6
  N3: MKR_GSM.D4_PWM, LCD.DB5
  N4: MKR_GSM.D5_PWM, LCD.DB4
  N5: MKR_GSM.D11_SDA, LCD.E
  N6: MKR_GSM.D12_SCL, LCD.RS
  N7: MKR_GSM.D13_RX, GPS.TXD
  N8: MKR_GSM.14_TX, GPS.RXD
  N9: MKR_GSM.GND, LCD.LED-
  5V: MKR_GSM.5V, LCD.VDD, GPS.VCC
  VSS: LCD.VSS, LCD.R/W, GPS.GND
  N10: LCD.V0, R1.Pin_1
  N11: LCD.LED+, R1.Pin_0

custom parts:
  Arduino MKR1000: MKR1000 is a powerful board that combines the functionality of the Zero and the Wi-Fi Shield. It is the ideal solution for makers wanting to design IoT projects with minimal previous experience in networking
